# Fritzing sketch George (saved by Fritzing 0.9.2b)
breadboards: 1

parts:
  Part1 = Arduino Uno (Rev3)
  Part2 = LED Matrix - Serial Interface - Red/Green/Blue
  DHT2 = DHT11_Temperature_and_Humitidy_Sensor
  R1 = Resistor [tolerance=±5% resistance=220 package="0402 [SMD]"]
  PIR2 = PIR sensor
  PIR3 = PIR sensor
  Part3 = Soil Moisture Sensor
  R2 = Photocell (LDR) [package=THT]
  R3 = Resistor [tolerance=±5% resistance=220 package="0603 [SMD]"]

nets:
  N1: Part1.D10_PWM/SS, Part2.SCK
  N2: Part1.D11_PWM/MOSI, Part2.CS
  N3: Part1.D12/MISO, Part2.MOSI
  VDD: Part1.D1/TX, Part1.5V, Part2.VCC, DHT2.connector1, R1.Pin_0, PIR2.VDD, PIR3.VDD, Part3.connector1, R2.pin_1, R3.Pin_0
  N4: Part1.D2, DHT2.connector2
  N5: Part1.D3_PWM, PIR2.SIG
  N6: Part1.D4, PIR3.SIG
  GND: Part1.GND, Part2.GND, DHT2.connector4, R1.Pin_1, PIR2.GND, PIR3.GND, Part3.connector2
  N7: R2.pin_0, R3.Pin_1
